# Fritzing sketch schema (saved by Fritzing 0.9.3b)
breadboards: 1

parts:
  Part1 = Arduino Uno (Rev3)
  Part2 = Breakout Board for Electret Microphone
  DFRobot_DFPlayer_Mini1 = DFRobot DFPlayer Mini [part_number=DFR0299]
  SP1 = SPEAKER [package=pcb_mount_speaker]
  R1 = Resistor [tolerance=±5% resistance=220 package="0402 [SMD]"]

nets:
  N1: Part1.A0, Part2.AUD
  N2: Part1.GND, DFRobot_DFPlayer_Mini1.GND-1, DFRobot_DFPlayer_Mini1.GND-2
  N3: Part1.D5_PWM, DFRobot_DFPlayer_Mini1.TX
  N4: Part1.D6_PWM, R1.Pin_0
  N5: Part1.5V, DFRobot_DFPlayer_Mini1.RX
  N6: DFRobot_DFPlayer_Mini1.VCC, R1.Pin_1
  N7: DFRobot_DFPlayer_Mini1.SPK_1, SP1.-
  N8: DFRobot_DFPlayer_Mini1.SPK_2, SP1.+

notes:
  The microphone part it's not the same used.
